// Logisim project circuit.circ as structural Verilog: 24 circuits, main circuit CPU
module CPU (
  output [7:0] out_1
);

  wire B0, B1, B2, B3, B4, B5, B6, B7, B8, B9, B10, B11, Clk, clock_1_out, D0, D1, D2, D3, D4, D5, D6, D7, E,
       E_Out, FGI, FGO, I, IEN, p, R, r_t, read_write_1_ld, read_write_1_str, S, T0, T1, T2, T3, T4, T5, T6,
       T7, T8, T9, T10, T11, T12, T13, T14, T15;
  wire [7:0] inpr_1_out_2;
  wire [15:0] AC, alu_16bit_1_alu_output, AR, bus_1_output, DR, IR, pc_1_out_25, ram_1_data, tr_1_out_5;

  Clock_part clock_1 (.out(clock_1_out));
  Clock clock_2 (.Pulse(clock_1_out), .S(S), .Clk(Clk));
  ALU_16bit alu_16bit_1 (
    .AC(AC), .DR(DR), .Input_E(E), .INPR(inpr_1_out_2), .ALU_Output(alu_16bit_1_alu_output), .T5(T5),
    .B11(B11), .B9(B9), .B7(B7), .B6(B6), .B5(B5), .D2(D2), .D1(D1), .D0(D0), .r(r_t), .p(p), .Output_E(E_Out));
  Read___Write read_write_1 (
    .T3(T3), .T6(T6), .T4(T4), .T1(T1), .I(I), .R(R), .D7(D7), .D6(D6), .D5(D5), .D2(D2), .D3(D3), .D1(D1),
    .D0(D0), .ld(read_write_1_ld), .str(read_write_1_str));
  PC pc_1 (
    .Input(bus_1_output), .out_25(pc_1_out_25), .T6(T6), .T5(T5), .T4(T4), .T2(T2), .T1(T1), .D6(D6),
    .D5(D5), .D4(D4), .B9(B9), .B8(B8), .B4(B4), .B3(B3), .B2(B2), .B1(B1), .R(R), .E(E), .r_2(r_t), .p(p),
    .FGI(FGI), .FGO(FGO), .CLK(Clk), .AC(AC), .DR(DR));
  INPR inpr_1 (.CLK(Clk), .out_2(inpr_1_out_2));
  IR ir_1 (.in_4(bus_1_output), .out_5(IR), .T1(T1), .R(R), .CLK(Clk));
  OUTR outr_1 (.B10(B10), .p(p), .CLK(Clk), .in_4(bus_1_output), .out_5(out_1));
  AR ar_1 (
    .in_10(bus_1_output), .out_11(AR), .T4(T4), .T3(T3), .T2(T2), .T0(T0), .D7(D7), .D5(D5), .I(I), .R(R),
    .CLK(Clk));
  DR dr_1 (.T5(T5), .T4(T4), .D6(D6), .D2(D2), .D1(D1), .D0(D0), .CLK(Clk), .in_2(bus_1_output), .out_9(DR));
  TR tr_1 (.in_4(bus_1_output), .out_5(tr_1_out_5), .T0(T0), .R(R), .CLK(Clk));
  Control_Unit control_unit_1 (
    .IR(IR), .D_i({D7, D6, D5, D4, D3, D2, D1, D0}), .p___r({r_t, p}),
    .B_i({B11, B10, B9, B8, B7, B6, B5, B4, B3, B2, B1, B0}),
    .T_i({T15, T14, T13, T12, T11, T10, T9, T8, T7, T6, T5, T4, T3, T2, T1, T0}), .SC_Input(4'b0000),
    .Flip_Flops({FGO, FGI, IEN, R, E, S, I}), .Clk(Clk), .E_Carry(E_Out));
  AC ac_1 (
    .in_2(alu_16bit_1_alu_output), .out_14(AC), .T5(T5), .B11(B11), .B9(B9), .B7(B7), .B6(B6), .B5(B5),
    .D2(D2), .D1(D1), .D0(D0), .r(r_t), .p(p), .CLK(Clk));
  RAM #(.addrWidth(12), .dataWidth(16), .bus("separate")) ram_1 (
    .addr(AR[11:0]), .din(bus_1_output), .data(ram_1_data), .str(read_write_1_str), .clk(Clk),
    .ld(read_write_1_ld));  // open: sel, clr
  Bus bus_1 (
    .PC(pc_1_out_25), .AC(AC), .TR(tr_1_out_5), .AR(AR), .DR(DR), .IR(IR), .M(ram_1_data),
    .Output(bus_1_output), .T6(T6), .T5(T5), .T4(T4), .T3(T3), .T2(T2), .T1(T1), .T0(T0), .D7(D7), .D6(D6),
    .D5(D5), .D4(D4), .D3(D3), .D2(D2), .D1(D1), .D0(D0), .R(R), .I(I), .p(p), .B10(B10));

  // Notes on the sheet:
  //   _
  //   _
  //   _
  //   _
  //   _
  //   CPU:
  //   _
  //   _
  //   _
  //   _
  //   _
  //   _
  //   _
  //   _
  //   _
  //   _
  //   Control Signals:
  //   _
  //   _
  //   _
  //   _
  //   _
  //   _
  //   _
  //   _
  //   _
  //   _
  //   _
  //   _
  //   _
  //   _
  //   _
  //   _
  //   _
  //   _
  //   _
  //   _
  //   _
  //   _
  //   _
  //   _
  //   _
  //   _
  //   _
  //   _
  //   _
  //   _
  //   _
  //   _
  //   _
  //   _
  //   _
  //   _
  //   _
  //   _
  //   _
  //   _
  //   _
  //   _
  //   _
  //   _
  //   _
  //   _
  //   _
  //   _
  //   _
  //   _
  //   _
  //   _
  //   _
  //   _
  //   _
  //   _
  //   _
  //   _
  //   _
  //   _
  //   _
  //   _
  //   _
endmodule

module Bus (
  input  [15:0] AR,
  input  [15:0] PC,
  input  T6,
  input  T5,
  input  T4,
  input  T3,
  input  T2,
  input  T1,
  input  T0,
  input  D7,
  input  D6,
  input  D5,
  input  D4,
  input  D3,
  input  D2,
  input  D1,
  input  D0,
  input  p,
  input  R,
  input  I,
  input  B10,
  input  [15:0] DR,
  input  [15:0] AC,
  input  [15:0] IR,
  input  [15:0] TR,
  input  [15:0] M,
  output [15:0] Output
);

  wire and_1_out, and_2_out, and_3_out, and_4_out, and_5_out, and_6_out, and_7_out, and_8_out, and_9_out,
       and_10_out, not_1_out, not_2_out, not_3_out, or_1_out, S0, S1, S2, x1, x2, x3, x4, x5, x6, x7;

  and and_1 (and_1_out, D4, T4);
  and and_2 (and_2_out, D5, T5);
  and and_3 (and_3_out, T4, D5);
  or u_AR (x1, and_1_out, and_2_out);
  or u_PC (x2, T0, and_3_out);
  and and_4 (and_4_out, D2, T5);
  or u_DR (x3, and_4_out, and_5_out);
  and and_5 (and_5_out, D6, T6);
  and and_6 (and_6_out, D3, T4);
  or u_AC (x4, and_6_out, and_7_out);
  and and_7 (and_7_out, p, B10);
  not not_1 (not_1_out, R);
  and and_8 (and_8_out, not_1_out, T1);
  not not_2 (not_2_out, D7);
  and and_9 (and_9_out, not_2_out, I, T3);
  and and_10 (and_10_out, T4, or_1_out);
  or or_1 (or_1_out, D0, D1, D2, D6);
  not not_3 (not_3_out, R);
  and u_IR (x5, not_3_out, T2);
  and u_TR (x6, R, T1);
  or Memory (x7, and_8_out, and_9_out, and_10_out);
  Priority_Encoder priority_encoder_1 (
    .in0(1'b0), .in1(x1), .in2(x2), .in3(x3), .in4(x4), .in5(x5), .in6(x6), .in7(x7), .out({S2, S1, S0}));  // open: en_in
  Multiplexer #(.select(3), .width(16), .enable("false")) multiplexer_1 (
    .in0({16{1'b0}}), .in1(AR), .in2(PC), .in3(DR), .in4(AC), .in5(IR), .in6(TR), .in7(M), .out(Output),
    .sel({S2, S1, S0}));

  // Other names for the same wires on the sheet: Out[15:0] = Output

  // Notes on the sheet:
  //   _
  //   _
  //   _
  //   _
  //   Control Gates:
  //   _
  //   _
  //   _
  //   _
  //   _
  //   _
  //   _
  //   _
  //   _
  //   _
  //   _
  //   _
  //   _
  //   _
  //   _
  //   _
  //   _
  //   _
  //   _
  //   _
  //   _
  //   _
  //   _
  //   _
  //   _
  //   _
  //   _
  //   _
  //   _
  //   _
  //   |
  //   |
  //   |
  //   |
  //   |
  //   |
  //   |
  //   _
  //   |
  //   |
  //   |
  //   |
  //   |
  //   |
  //   _
  //   |
  //   |
  //   |
  //   |
  //   |
  //   |
  //   |
  //   _
  //   _
  //   _
  //   _
  //   |
  //   |
  //   |
  //   _
  //   Encoder:
  //   _
  //   _
  //   _
  //   _
  //   _
  //   Bus:
  //   _
  //   _
  //   _
  //   _
  //   _
  //   _
  //   _
  //   _
  //   _
  //   _
  //   _
  //   _
  //   _
  //   _
  //   _
  //   _
  //   _
  //   _
  //   _
  //   _
  //   Input/Output:
  //   _
  //   _
  //   _
  //   _
  //   _
  //   _
  //   _
  //   _
  //   _
  //   _
  //   _
  //   _
  //   _
  //   _
  //   _
  //   _
  //   _
  //   _
  //   _
  //   _
  //   _
  //   _
  //   _
  //   _
  //   _
  //   _
  //   _
  //   _
  //   _
  //   _
  //   _
  //   _
  //   _
  //   _
  //   _
  //   _
  //   _
  //   _
  //   _
  //   _
  //   _
  //   _
  //   _
endmodule

module Clock (
  input  Pulse,
  input  S,
  output Clk
);

  wire d_ff_1_qn;

  D_Flip_Flop d_ff_1 (.clk(Pulse), .D(S), .Qn(d_ff_1_qn));  // open: Q, preset, en, reset
  and and_1 (Clk, Pulse, d_ff_1_qn);

  // Notes on the sheet:
  //   Clock:
endmodule

module Control_Unit (
  input  [15:0] IR,
  input  [3:0] SC_Input,
  input  Clk,
  input  E_Carry,
  output [7:0] D_i,
  output [11:0] B_i,
  output [1:0] p___r,
  output [15:0] T_i,
  output [6:0] Flip_Flops
);

  wire not_1_out;
  wire [3:0] sc_1_out;

  Decoder #(.select(3), .enable("false")) decoder_1 (
    .out0(D_i[0]), .out1(D_i[1]), .out2(D_i[2]), .out3(D_i[3]), .out4(D_i[4]), .out5(D_i[5]), .out6(D_i[6]),
    .out7(D_i[7]), .sel(IR[14:12]));
  SC sc_1 (
    .T6(T_i[6]), .T5(T_i[5]), .T4(T_i[4]), .T2(T_i[2]), .D6(D_i[6]), .D5(D_i[5]), .D4(D_i[4]), .D3(D_i[3]),
    .D2(D_i[2]), .D1(D_i[1]), .D0(D_i[0]), .R(Flip_Flops[3]), .r_2(p___r[1]), .p(p___r[0]), .CLK(Clk),
    .In(SC_Input), .Out(sc_1_out));
  I i_1 (.CLK(Clk), .out_5(Flip_Flops[0]), .T2(T_i[2]), .R(Flip_Flops[3]), .IR_15(IR[15]));
  FGI fgi_1 (.CLK(Clk), .out_4(Flip_Flops[5]), .B11(IR[11]), .p(p___r[0]));
  S s_1 (.CLK(Clk), .out_4(Flip_Flops[1]), .B0(IR[0]), .r(p___r[1]));
  FGO fgo_1 (.CLK(Clk), .out_4(Flip_Flops[6]), .B10(IR[10]), .p(p___r[0]));
  and p (p___r[0], T_i[3], D_i[7], Flip_Flops[0]);
  and r (p___r[1], T_i[3], D_i[7], not_1_out);
  E e_1 (
    .CLK(Clk), .out_10(Flip_Flops[2]), .B10(IR[10]), .B8(IR[8]), .r(p___r[1]), .E_Out(E_Carry), .B6(IR[6]),
    .B7(IR[7]), .T5(T_i[5]), .D1(D_i[1]));
  not not_1 (not_1_out, Flip_Flops[0]);
  Decoder #(.select(4), .enable("false")) decoder_2 (
    .out0(T_i[0]), .out1(T_i[1]), .out2(T_i[2]), .out3(T_i[3]), .out4(T_i[4]), .out5(T_i[5]), .out6(T_i[6]),
    .out7(T_i[7]), .out8(T_i[8]), .out9(T_i[9]), .out10(T_i[10]), .out11(T_i[11]), .out12(T_i[12]),
    .out13(T_i[13]), .out14(T_i[14]), .out15(T_i[15]), .sel(sc_1_out));
  IEN ien_1 (.CLK(Clk), .out_7(Flip_Flops[4]), .T2(T_i[2]), .B6(IR[6]), .B7(IR[7]), .p(p___r[0]), .R(Flip_Flops[3]));
  R r_2 (
    .CLK(Clk), .out_9(Flip_Flops[3]), .T0(T_i[0]), .T1(T_i[1]), .T2(T_i[2]), .R(Flip_Flops[3]),
    .IEN(Flip_Flops[4]), .FGI(Flip_Flops[5]), .FGO(Flip_Flops[6]));

  assign B_i = IR[11:0];

  // Other names for the same wires on the sheet: B0 = IR[0]; B1 = IR[1]; B2 = IR[2]; B3 = IR[3]; B4 = IR[4];
  //   B5 = IR[5]; B6 = IR[6]; B7 = IR[7]; B8 = IR[8]; B9 = IR[9]; B10 = IR[10]; B11 = IR[11]; D0 = D_i[0];
  //   D1 = D_i[1]; D2 = D_i[2]; D3 = D_i[3]; D4 = D_i[4]; D5 = D_i[5]; D6 = D_i[6]; D7 = D_i[7]; I = Flip_Flops[0];
  //   S = Flip_Flops[1]; E = Flip_Flops[2]; R = Flip_Flops[3]; IEN = Flip_Flops[4]; FGI = Flip_Flops[5];
  //   FGO = Flip_Flops[6]; IR_15 = IR[15]; p = p___r[0]; r_t = p___r[1]; T0 = T_i[0]; T1 = T_i[1]; T2 = T_i[2];
  //   T3 = T_i[3]; T4 = T_i[4]; T5 = T_i[5]; T6 = T_i[6]; T7 = T_i[7]; T8 = T_i[8]; T9 = T_i[9]; T10 = T_i[10];
  //   T11 = T_i[11]; T12 = T_i[12]; T13 = T_i[13]; T14 = T_i[14]; T15 = T_i[15]

  // Notes on the sheet:
  //   _
  //   _
  //   _
  //   _
  //   _
  //   Control Inputs:
  //   _
  //   _
  //   _
  //   _
  //   _
  //   Flip-Flops:
  //   Operation Decoder
  //   Sequence Counter
  //   _
  //   _
  //   _
  //   _
  //   _
  //   _
  //   _
  //   _
  //   _
  //   _
  //   _
  //   _
  //   _
  //   _
  //   _
  //   _
  //   _
  //   _
  //   _
  //   _
  //   _
  //   _
  //   _
  //   _
  //   _
  //   |
  //   |
  //   |
  //   |
  //   |
  //   |
  //   |
  //   |
  //   |
  //   |
  //   |
  //   |
  //   |
  //   |
  //   |
  //   |
  //   _
  //   Timing Decoder
  //   _
  //   _
  //   _
  //   _
  //   _
  //   _
  //   _
  //   _
  //   _
  //   _
  //   _
  //   _
  //   _
  //   _
  //   _
  //   Control Outputs:
  //   _
  //   _
  //   _
  //   _
  //   _
  //   _
  //   _
  //   _
  //   _
  //   _
  //   _
  //   _
  //   _
  //   _
  //   _
  //   _
  //   _
  //   _
  //   _
  //   _
  //   _
  //   _
  //   |
  //   |
  //   |
  //   |
  //   |
  //   |
  //   |
  //   |
  //   |
  //   _
  //   _
  //   _
  //   |
  //   |
  //   |
  //   |
  //   |
  //   |
  //   |
  //   |
  //   |
endmodule

module Read___Write (
  input  T6,
  input  T4,
  input  T3,
  input  T1,
  input  R,
  input  I,
  input  D7,
  input  D6,
  input  D5,
  input  D3,
  input  D2,
  input  D1,
  input  D0,
  output ld,
  output str
);

  wire and_1_out, and_2_out, and_3_out, and_4_out, and_5_out, and_6_out, and_7_out, not_1_out, not_2_out,
       or_1_out;

  not not_1 (not_1_out, R);
  not not_2 (not_2_out, D7);
  or or_1 (or_1_out, D0, D1, D2, D6);
  and and_1 (and_1_out, R, T1);
  and and_2 (and_2_out, D3, T4);
  and and_3 (and_3_out, D5, T4);
  and and_4 (and_4_out, D6, T6);
  and and_5 (and_5_out, not_1_out, T1);
  and and_6 (and_6_out, not_2_out, I, T3);
  and and_7 (and_7_out, T4, or_1_out);
  or u_ld (ld, and_5_out, and_6_out, and_7_out);
  or u_str (str, and_1_out, and_2_out, and_3_out, and_4_out);

  // Notes on the sheet:
  //   _
  //   _
  //   _
  //   _
  //   _
  //   _
  //   _
  //   _
  //   _
  //   _
  //   Write to Memory/ str:
  //   Read From Memory/ ld:
  //   _
  //   _
  //   _
  //   _
  //   _
  //   _
  //   _
  //   _
  //   _
  //   _
  //   _
  //   _
  //   _
  //   _
  //   _
  //   _
  //   _
  //   _
  //   _
  //   _
  //   _
  //   _
endmodule

module AR (
  input  CLK,
  input  T4,
  input  T3,
  input  T2,
  input  T0,
  input  D7,
  input  D5,
  input  I,
  input  R,
  input  [15:0] in_10,
  output [15:0] out_11
);

  wire and_1_out, and_2_out, and_3_out, CLR, INR, LD, not_1_out, not_2_out, not_3_out;

  not not_1 (not_1_out, R);
  not not_2 (not_2_out, R);
  not not_3 (not_3_out, D7);
  and u_INR (INR, D5, T4);
  and and_1 (and_1_out, not_1_out, T0);
  and and_2 (and_2_out, not_2_out, T2);
  and and_3 (and_3_out, not_3_out, I, T3);
  or u_LD (LD, and_1_out, and_2_out, and_3_out);
  and u_CLR (CLR, R, T0);
  Counter #(.width(12), .max('hfff)) counter_1 (
    .load(LD), .D(in_10[11:0]), .count(INR), .Q(out_11[11:0]), .clk(CLK), .clr(CLR));  // open: carry

  assign out_11[15:12] = 4'b0000;

  // Other names for the same wires on the sheet: In[11:0] = in_10[11:0]; Out[11:0] = out_11[11:0]

  // Notes on the sheet:
  //   Control Gates:
  //   |
  //   |
  //   |
  //   |
  //   |
  //   |
  //   |
  //   |
  //   |
  //   |
  //   _
  //   _
  //   _
  //   _
  //   |
  //   |
  //   |
  //   |
  //   |
  //   |
  //   |
  //   |
  //   |
  //   Address Register:
  //   _
  //   _
  //   _
  //   _
  //   Input/Output:
  //   _
  //   _
  //   _
  //   _
  //   _
  //   _
  //   _
  //   _
  //   _
  //   _
  //   _
  //   _
  //   _
  //   _
  //   _
  //   _
  //   _
  //   _
endmodule

module PC (
  input  CLK,
  input  [15:0] AC,
  input  [15:0] DR,
  input  [15:0] Input,
  input  T6,
  input  T5,
  input  T4,
  input  T2,
  input  T1,
  input  D6,
  input  D5,
  input  D4,
  input  B9,
  input  B8,
  input  B4,
  input  B3,
  input  B2,
  input  B1,
  input  R,
  input  E,
  input  r_2,
  input  p,
  input  FGI,
  input  FGO,
  output [15:0] out_25
);

  wire AC_t, and_1_out, and_2_out, and_3_out, and_4_out, and_5_out, and_6_out, and_7_out, and_8_out,
       and_9_out, and_10_out, and_11_out, CLR, DR_t, INR, LD, not_1_out, not_2_out, not_3_out, not_4_out,
       not_5_out;

  and and_1 (and_1_out, D4, T4);
  and and_2 (and_2_out, D5, T5);
  or u_LD (LD, and_1_out, and_2_out);
  and u_CLR (CLR, R, T1);
  and and_3 (and_3_out, R, T2);
  not not_1 (not_1_out, R);
  and and_4 (and_4_out, not_1_out, T1);
  not not_2 (not_2_out, DR_t);
  and and_5 (and_5_out, not_2_out, D6, T6);
  not not_3 (not_3_out, AC[15]);
  and and_6 (and_6_out, not_3_out, r_2, B4);
  and and_7 (and_7_out, AC[15], r_2, B3);
  not not_4 (not_4_out, AC_t);
  and and_8 (and_8_out, not_4_out, r_2, B2);
  not not_5 (not_5_out, E);
  and and_9 (and_9_out, not_5_out, r_2, B1);
  and and_10 (and_10_out, FGI, p, B9);
  and and_11 (and_11_out, FGO, p, B8);
  or u_INR (INR, and_3_out, and_4_out, and_5_out, and_6_out, and_7_out, and_8_out, and_9_out, and_10_out, and_11_out);
  or or_1 (AC_t, AC[15], AC[14], AC[13], AC[12], AC[11], AC[10], AC[9], AC[8], AC[7], AC[6], AC[5], AC[4], AC[3], AC[2], AC[1], AC[0]);
  Counter #(.width(12), .max('hfff)) counter_1 (
    .load(LD), .D(Input[11:0]), .count(INR), .Q(out_25[11:0]), .clk(CLK), .clr(CLR));  // open: carry
  or or_2 (DR_t, DR[15], DR[14], DR[13], DR[12], DR[11], DR[10], DR[9], DR[8], DR[7], DR[6], DR[5], DR[4], DR[3], DR[2], DR[1], DR[0]);

  assign out_25[15:12] = 4'b0000;

  // Other names for the same wires on the sheet: AC_15 = AC[15]; In[11:0] = Input[11:0]; Out[11:0] = out_25[11:0];
  //   r_t = r_2

  // Notes on the sheet:
  //   Control Gates:
  //   |
  //   |
  //   |
  //   |
  //   |
  //   |
  //   |
  //   _
  //   _
  //   |
  //   |
  //   |
  //   |
  //   |
  //   |
  //   |
  //   |
  //   |
  //   |
  //   |
  //   |
  //   |
  //   |
  //   |
  //   |
  //   |
  //   |
  //   _
  //   _
  //   _
  //   _
  //   _
  //   Program Counter:
  //   _
  //   _
  //   _
  //   _
  //   _
  //   Input/Output:
  //   _
  //   _
  //   _
  //   _
  //   _
  //   _
  //   _
  //   _
  //   _
  //   _
  //   _
  //   _
  //   _
  //   _
endmodule

module DR (
  input  CLK,
  input  [15:0] in_2,
  input  T5,
  input  T4,
  input  D6,
  input  D2,
  input  D1,
  input  D0,
  output [15:0] out_9
);

  wire and_1_out, and_2_out, and_3_out, and_4_out, INR, LD;

  and u_INR (INR, D6, T5);
  and and_1 (and_1_out, D0, T4);
  and and_2 (and_2_out, D1, T4);
  and and_3 (and_3_out, D2, T4);
  and and_4 (and_4_out, D6, T4);
  or u_LD (LD, and_1_out, and_2_out, and_3_out, and_4_out);
  Counter #(.width(16), .max('hffff)) counter_1 (
    .load(LD), .D(in_2), .count(INR), .Q(out_9), .clk(CLK), .clr(1'b0));  // open: carry

  // Other names for the same wires on the sheet: In[15:0] = in_2; Out[15:0] = out_9

  // Notes on the sheet:
  //   Control Gates:
  //   |
  //   |
  //   |
  //   |
  //   |
  //   |
  //   |
  //   |
  //   |
  //   |
  //   _
  //   _
  //   _
  //   _
  //   |
  //   |
  //   |
  //   |
  //   |
  //   |
  //   |
  //   |
  //   |
  //   Data Register:
  //   _
  //   _
  //   _
  //   _
  //   _
  //   Input/Output:
  //   _
  //   _
  //   _
  //   _
  //   _
  //   _
  //   _
endmodule

module AC (
  input  CLK,
  input  [15:0] in_2,
  input  T5,
  input  B11,
  input  B9,
  input  B7,
  input  B6,
  input  B5,
  input  D2,
  input  D1,
  input  D0,
  input  r,
  input  p,
  output [15:0] out_14
);

  wire ADD_out, AND_out, CLR, COM_out, DR_out, INPR_out, INR, LD, SHL_out, SHR_out;

  and u_CLR (CLR, r, B11);
  and u_INR (INR, r, B5);
  and AND (AND_out, D0, T5);
  and ADD (ADD_out, D1, T5);
  and DR (DR_out, D2, T5);
  and INPR (INPR_out, p, B11);
  and COM (COM_out, r, B9);
  and SHR (SHR_out, r, B7);
  and SHL (SHL_out, r, B6);
  or u_LD (LD, AND_out, ADD_out, DR_out, INPR_out, COM_out, SHR_out, SHL_out);
  Counter #(.width(16), .max('hffff)) counter_1 (
    .load(LD), .D(in_2), .count(INR), .Q(out_14), .clk(CLK), .clr(CLR));  // open: carry

  // Other names for the same wires on the sheet: In[15:0] = in_2; Out[15:0] = out_14

  // Notes on the sheet:
  //   Control Gates:
  //   |
  //   |
  //   |
  //   |
  //   |
  //   |
  //   |
  //   |
  //   |
  //   |
  //   _
  //   _
  //   |
  //   |
  //   |
  //   |
  //   |
  //   |
  //   |
  //   |
  //   |
  //   Accumulator:
  //   _
  //   _
  //   _
  //   _
  //   _
  //   _
  //   _
  //   _
  //   _
  //   _
  //   Input/Output:
  //   _
  //   _
  //   _
  //   _
endmodule

module FA (
  input  A,
  input  B,
  input  Carry_In,
  output SUM,
  output Carry_Out
);

  wire and_1_out, and_2_out, xor_1_out;

  xor xor_1 (xor_1_out, A, B);
  and and_1 (and_1_out, Carry_In, xor_1_out);
  and and_2 (and_2_out, A, B);
  xor xor_2 (SUM, xor_1_out, Carry_In);
  or or_1 (Carry_Out, and_1_out, and_2_out);

  // Notes on the sheet:
  //   Full Adder:
endmodule

module ALU_1bit (
  input  C_i,
  input  AC_i_1,
  input  AC_i_1_2,
  input  AC_i,
  input  DR_i,
  input  INPR_i,
  input  AND_CTRL,
  input  ADD_CTRL,
  input  DR_CTRL,
  input  INPR_CTRL,
  input  COM_CTRL,
  input  SHR_CTRL,
  input  SHL_CTRL,
  output C_i_1,
  output I_i
);

  wire ADD_out, AND_out, COM_out, DR_out, fa_1_sum, INPR_out, not_1_out, SHL_out, SHR_out;

  FA fa_1 (.A(AC_i), .B(DR_i), .Carry_In(C_i), .SUM(fa_1_sum), .Carry_Out(C_i_1));
  not not_1 (not_1_out, AC_i);
  and AND (AND_out, AND_CTRL, AC_i, DR_i);
  and ADD (ADD_out, ADD_CTRL, fa_1_sum);
  and DR (DR_out, DR_CTRL, DR_i);
  and INPR (INPR_out, INPR_CTRL, INPR_i);
  and COM (COM_out, COM_CTRL, not_1_out);
  and SHR (SHR_out, SHR_CTRL, AC_i_1_2);
  and SHL (SHL_out, SHL_CTRL, AC_i_1);
  or or_1 (I_i, AND_out, ADD_out, DR_out, INPR_out, COM_out, SHR_out, SHL_out);

  // Notes on the sheet:
  //   1 Bit ALU:
endmodule

module ALU_16bit (
  input  Input_E,
  input  [15:0] AC,
  input  [7:0] INPR,
  input  [15:0] DR,
  input  T5,
  input  B11,
  input  B9,
  input  B7,
  input  B6,
  input  B5,
  input  D2,
  input  D1,
  input  D0,
  input  r,
  input  p,
  output Output_E,
  output [15:0] ALU_Output
);

  wire ADD_CTRL, and_1_out, and_2_out, and_3_out, AND_CTRL, bit0_c_i_1, bit1_c_i_1, bit2_c_i_1, bit3_c_i_1,
       bit4_c_i_1, bit5_c_i_1, bit6_c_i_1, bit7_c_i_1, bit8_c_i_1, bit9_c_i_1, bit10_c_i_1, bit11_c_i_1,
       bit12_c_i_1, bit13_c_i_1, bit14_c_i_1, COM_CTRL, DR_CTRL, E_Carry, INPR_CTRL, SHL_CTRL, SHR_CTRL;

  ALU_1bit bit0 (
    .AND_CTRL(AND_CTRL), .ADD_CTRL(ADD_CTRL), .DR_CTRL(DR_CTRL), .INPR_CTRL(INPR_CTRL), .COM_CTRL(COM_CTRL),
    .SHR_CTRL(SHR_CTRL), .SHL_CTRL(SHL_CTRL), .I_i(ALU_Output[0]), .C_i(1'b0), .AC_i_1(Input_E),
    .AC_i_1_2(AC[1]), .AC_i(AC[0]), .DR_i(DR[0]), .INPR_i(INPR[0]), .C_i_1(bit0_c_i_1));
  ALU_1bit bit7 (
    .AND_CTRL(AND_CTRL), .ADD_CTRL(ADD_CTRL), .DR_CTRL(DR_CTRL), .INPR_CTRL(INPR_CTRL), .COM_CTRL(COM_CTRL),
    .SHR_CTRL(SHR_CTRL), .SHL_CTRL(SHL_CTRL), .I_i(ALU_Output[7]), .C_i(bit6_c_i_1), .AC_i_1(AC[6]),
    .AC_i_1_2(AC[8]), .AC_i(AC[7]), .DR_i(DR[7]), .INPR_i(INPR[7]), .C_i_1(bit7_c_i_1));
  ALU_1bit bit8 (
    .AND_CTRL(AND_CTRL), .ADD_CTRL(ADD_CTRL), .DR_CTRL(DR_CTRL), .INPR_CTRL(INPR_CTRL), .COM_CTRL(COM_CTRL),
    .SHR_CTRL(SHR_CTRL), .SHL_CTRL(SHL_CTRL), .I_i(ALU_Output[8]), .C_i(bit7_c_i_1), .AC_i_1(AC[7]),
    .AC_i_1_2(AC[9]), .AC_i(AC[8]), .DR_i(DR[8]), .INPR_i(1'b0), .C_i_1(bit8_c_i_1));
  ALU_1bit bit15 (
    .AND_CTRL(AND_CTRL), .ADD_CTRL(ADD_CTRL), .DR_CTRL(DR_CTRL), .INPR_CTRL(INPR_CTRL), .COM_CTRL(COM_CTRL),
    .SHR_CTRL(SHR_CTRL), .SHL_CTRL(SHL_CTRL), .I_i(ALU_Output[15]), .C_i(bit14_c_i_1), .AC_i_1(AC[14]),
    .AC_i_1_2(Input_E), .AC_i(AC[15]), .DR_i(DR[15]), .INPR_i(1'b0), .C_i_1(E_Carry));
  ALU_1bit bit1 (
    .AND_CTRL(AND_CTRL), .ADD_CTRL(ADD_CTRL), .DR_CTRL(DR_CTRL), .INPR_CTRL(INPR_CTRL), .COM_CTRL(COM_CTRL),
    .SHR_CTRL(SHR_CTRL), .SHL_CTRL(SHL_CTRL), .I_i(ALU_Output[1]), .C_i(bit0_c_i_1), .AC_i_1(AC[0]),
    .AC_i_1_2(AC[2]), .AC_i(AC[1]), .DR_i(DR[1]), .INPR_i(INPR[1]), .C_i_1(bit1_c_i_1));
  ALU_1bit bit6 (
    .AND_CTRL(AND_CTRL), .ADD_CTRL(ADD_CTRL), .DR_CTRL(DR_CTRL), .INPR_CTRL(INPR_CTRL), .COM_CTRL(COM_CTRL),
    .SHR_CTRL(SHR_CTRL), .SHL_CTRL(SHL_CTRL), .I_i(ALU_Output[6]), .C_i(bit5_c_i_1), .AC_i_1(AC[5]),
    .AC_i_1_2(AC[7]), .AC_i(AC[6]), .DR_i(DR[6]), .INPR_i(INPR[6]), .C_i_1(bit6_c_i_1));
  ALU_1bit bit9 (
    .AND_CTRL(AND_CTRL), .ADD_CTRL(ADD_CTRL), .DR_CTRL(DR_CTRL), .INPR_CTRL(INPR_CTRL), .COM_CTRL(COM_CTRL),
    .SHR_CTRL(SHR_CTRL), .SHL_CTRL(SHL_CTRL), .I_i(ALU_Output[9]), .C_i(bit8_c_i_1), .AC_i_1(AC[8]),
    .AC_i_1_2(AC[10]), .AC_i(AC[9]), .DR_i(DR[9]), .INPR_i(1'b0), .C_i_1(bit9_c_i_1));
  ALU_1bit bit14 (
    .AND_CTRL(AND_CTRL), .ADD_CTRL(ADD_CTRL), .DR_CTRL(DR_CTRL), .INPR_CTRL(INPR_CTRL), .COM_CTRL(COM_CTRL),
    .SHR_CTRL(SHR_CTRL), .SHL_CTRL(SHL_CTRL), .I_i(ALU_Output[14]), .C_i(bit13_c_i_1), .AC_i_1(AC[13]),
    .AC_i_1_2(AC[15]), .AC_i(AC[14]), .DR_i(DR[14]), .INPR_i(1'b0), .C_i_1(bit14_c_i_1));
  and and_1 (and_1_out, AC[15], SHL_CTRL);
  ALU_1bit bit2 (
    .AND_CTRL(AND_CTRL), .ADD_CTRL(ADD_CTRL), .DR_CTRL(DR_CTRL), .INPR_CTRL(INPR_CTRL), .COM_CTRL(COM_CTRL),
    .SHR_CTRL(SHR_CTRL), .SHL_CTRL(SHL_CTRL), .I_i(ALU_Output[2]), .C_i(bit1_c_i_1), .AC_i_1(AC[1]),
    .AC_i_1_2(AC[3]), .AC_i(AC[2]), .DR_i(DR[2]), .INPR_i(INPR[2]), .C_i_1(bit2_c_i_1));
  ALU_1bit bit5 (
    .AND_CTRL(AND_CTRL), .ADD_CTRL(ADD_CTRL), .DR_CTRL(DR_CTRL), .INPR_CTRL(INPR_CTRL), .COM_CTRL(COM_CTRL),
    .SHR_CTRL(SHR_CTRL), .SHL_CTRL(SHL_CTRL), .I_i(ALU_Output[5]), .C_i(bit4_c_i_1), .AC_i_1(AC[4]),
    .AC_i_1_2(AC[6]), .AC_i(AC[5]), .DR_i(DR[5]), .INPR_i(INPR[5]), .C_i_1(bit5_c_i_1));
  ALU_1bit bit10 (
    .AND_CTRL(AND_CTRL), .ADD_CTRL(ADD_CTRL), .DR_CTRL(DR_CTRL), .INPR_CTRL(INPR_CTRL), .COM_CTRL(COM_CTRL),
    .SHR_CTRL(SHR_CTRL), .SHL_CTRL(SHL_CTRL), .I_i(ALU_Output[10]), .C_i(bit9_c_i_1), .AC_i_1(AC[9]),
    .AC_i_1_2(AC[11]), .AC_i(AC[10]), .DR_i(DR[10]), .INPR_i(1'b0), .C_i_1(bit10_c_i_1));
  ALU_1bit bit13 (
    .AND_CTRL(AND_CTRL), .ADD_CTRL(ADD_CTRL), .DR_CTRL(DR_CTRL), .INPR_CTRL(INPR_CTRL), .COM_CTRL(COM_CTRL),
    .SHR_CTRL(SHR_CTRL), .SHL_CTRL(SHL_CTRL), .I_i(ALU_Output[13]), .C_i(bit12_c_i_1), .AC_i_1(AC[12]),
    .AC_i_1_2(AC[14]), .AC_i(AC[13]), .DR_i(DR[13]), .INPR_i(1'b0), .C_i_1(bit13_c_i_1));
  or or_1 (Output_E, and_1_out, and_2_out, and_3_out);
  and and_2 (and_2_out, AC[0], SHR_CTRL);
  and and_3 (and_3_out, E_Carry, ADD_CTRL);
  ALU_1bit bit3 (
    .AND_CTRL(AND_CTRL), .ADD_CTRL(ADD_CTRL), .DR_CTRL(DR_CTRL), .INPR_CTRL(INPR_CTRL), .COM_CTRL(COM_CTRL),
    .SHR_CTRL(SHR_CTRL), .SHL_CTRL(SHL_CTRL), .I_i(ALU_Output[3]), .C_i(bit2_c_i_1), .AC_i_1(AC[2]),
    .AC_i_1_2(AC[4]), .AC_i(AC[3]), .DR_i(DR[3]), .INPR_i(INPR[3]), .C_i_1(bit3_c_i_1));
  ALU_1bit bit4 (
    .AND_CTRL(AND_CTRL), .ADD_CTRL(ADD_CTRL), .DR_CTRL(DR_CTRL), .INPR_CTRL(INPR_CTRL), .COM_CTRL(COM_CTRL),
    .SHR_CTRL(SHR_CTRL), .SHL_CTRL(SHL_CTRL), .I_i(ALU_Output[4]), .C_i(bit3_c_i_1), .AC_i_1(AC[3]),
    .AC_i_1_2(AC[5]), .AC_i(AC[4]), .DR_i(DR[4]), .INPR_i(INPR[4]), .C_i_1(bit4_c_i_1));
  ALU_1bit bit11 (
    .AND_CTRL(AND_CTRL), .ADD_CTRL(ADD_CTRL), .DR_CTRL(DR_CTRL), .INPR_CTRL(INPR_CTRL), .COM_CTRL(COM_CTRL),
    .SHR_CTRL(SHR_CTRL), .SHL_CTRL(SHL_CTRL), .I_i(ALU_Output[11]), .C_i(bit10_c_i_1), .AC_i_1(AC[10]),
    .AC_i_1_2(AC[12]), .AC_i(AC[11]), .DR_i(DR[11]), .INPR_i(1'b0), .C_i_1(bit11_c_i_1));
  ALU_1bit bit12 (
    .AND_CTRL(AND_CTRL), .ADD_CTRL(ADD_CTRL), .DR_CTRL(DR_CTRL), .INPR_CTRL(INPR_CTRL), .COM_CTRL(COM_CTRL),
    .SHR_CTRL(SHR_CTRL), .SHL_CTRL(SHL_CTRL), .I_i(ALU_Output[12]), .C_i(bit11_c_i_1), .AC_i_1(AC[11]),
    .AC_i_1_2(AC[13]), .AC_i(AC[12]), .DR_i(DR[12]), .INPR_i(1'b0), .C_i_1(bit12_c_i_1));
  and and_4 (AND_CTRL, D0, T5);
  and and_5 (ADD_CTRL, D1, T5);
  and and_6 (DR_CTRL, D2, T5);
  and and_7 (INPR_CTRL, p, B11);
  and and_8 (COM_CTRL, r, B9);
  and and_9 (SHR_CTRL, r, B7);
  and and_10 (SHL_CTRL, r, B6);

  // Other names for the same wires on the sheet: I0 = ALU_Output[0]; I1 = ALU_Output[1]; I2 = ALU_Output[2];
  //   I3 = ALU_Output[3]; I4 = ALU_Output[4]; I5 = ALU_Output[5]; I6 = ALU_Output[6]; I7 = ALU_Output[7];
  //   I8 = ALU_Output[8]; I9 = ALU_Output[9]; I10 = ALU_Output[10]; I11 = ALU_Output[11]; I12 = ALU_Output[12];
  //   I13 = ALU_Output[13]; I14 = ALU_Output[14]; I15 = ALU_Output[15]; E = Input_E

  // Notes on the sheet:
  //   _
  //   _
  //   _
  //   _
  //   _
  //   16 Bit ALU:
  //   _
  //   _
  //   _
  //   _
  //   _
  //   Input/Output:
  //   _
  //   _
  //   _
  //   _
  //   _
  //   _
  //   _
  //   _
  //   _
  //   _
  //   _
  //   _
  //   _
  //   _
  //   _
  //   _
  //   _
  //   _
  //   _
  //   _
  //   _
  //   _
  //   _
  //   _
  //   _
  //   _
  //   _
  //   _
  //   _
  //   _
  //   _
  //   _
  //   _
  //   _
  //   _
  //   _
  //   _
  //   _
  //   _
  //   _
  //   _
  //   _
  //   _
  //   _
  //   _
  //   _
  //   _
  //   _
  //   _
  //   _
  //   _
  //   _
  //   _
  //   _
  //   _
  //   _
  //   _
  //   _
  //   _
  //   _
  //   _
  //   _
  //   _
  //   _
  //   _
  //   _
  //   _
  //   _
  //   _
  //   _
  //   _
  //   _
  //   _
  //   _
  //   _
  //   _
  //   _
  //   _
  //   |
  //   |
  //   |
  //   |
  //   |
  //   |
  //   |
  //   |
  //   |
  //   |
  //   |
  //   |
  //   |
  //   |
  //   |
  //   |
  //   |
  //   |
  //   |
  //   _
  //   _
  //   _
  //   _
  //   _
  //   _
  //   _
  //   _
  //   _
  //   _
  //   Controllers:
  //   _
  //   _
  //   _
  //   _
  //   _
  //   _
  //   _
  //   _
  //   _
  //   _
  //   _
  //   _
  //   _
  //   _
  //   _
  //   _
  //   _
  //   _
  //   _
  //   _
endmodule

module TR (
  input  CLK,
  input  T0,
  input  R,
  input  [15:0] in_4,
  output [15:0] out_5
);

  wire LD, not_1_out;

  not not_1 (not_1_out, R);
  and u_LD (LD, not_1_out, T0);
  Counter #(.width(16), .max('hffff)) counter_1 (
    .load(LD), .D(in_4), .count(1'b0), .Q(out_5), .clk(CLK), .clr(1'b0));  // open: carry

  // Other names for the same wires on the sheet: In[15:0] = in_4; Out[15:0] = out_5

  // Notes on the sheet:
  //   Control Gates:
  //   |
  //   |
  //   |
  //   |
  //   |
  //   |
  //   |
  //   |
  //   |
  //   |
  //   _
  //   _
  //   |
  //   |
  //   |
  //   |
  //   |
  //   |
  //   |
  //   |
  //   |
  //   _
  //   _
  //   _
  //   _
  //   _
  //   Temporary Register:
  //   _
  //   _
  //   _
  //   _
  //   _
  //   Input/Output:
  //   _
  //   _
  //   _
  //   _
  //   _
  //   _
endmodule

module IR (
  input  CLK,
  input  T1,
  input  R,
  input  [15:0] in_4,
  output [15:0] out_5
);

  wire LD, not_1_out;

  not not_1 (not_1_out, R);
  and u_LD (LD, not_1_out, T1);
  Counter #(.width(16), .max('hffff)) counter_1 (
    .load(LD), .D(in_4), .count(1'b0), .Q(out_5), .clk(CLK), .clr(1'b0));  // open: carry

  // Other names for the same wires on the sheet: In[15:0] = in_4; Out[15:0] = out_5

  // Notes on the sheet:
  //   Control Gates:
  //   |
  //   |
  //   |
  //   |
  //   |
  //   |
  //   |
  //   |
  //   |
  //   |
  //   _
  //   |
  //   |
  //   |
  //   |
  //   |
  //   |
  //   |
  //   |
  //   |
  //   _
  //   _
  //   _
  //   _
  //   _
  //   Instruction Register:
  //   _
  //   _
  //   _
  //   _
  //   _
  //   Input/Output:
  //   _
  //   _
  //   _
  //   _
  //   _
endmodule

module OUTR (
  input  CLK,
  input  B10,
  input  p,
  input  [15:0] in_4,
  output [7:0] out_5
);

  wire LD;

  and u_LD (LD, p, B10);
  Counter counter_1 (.load(LD), .D(in_4[7:0]), .count(1'b0), .Q(out_5), .clk(CLK), .clr(1'b0));  // open: carry

  // Other names for the same wires on the sheet: In[7:0] = in_4[7:0]; Out[7:0] = out_5

  // Notes on the sheet:
  //   Control Gates:
  //   |
  //   |
  //   |
  //   |
  //   |
  //   |
  //   |
  //   |
  //   |
  //   |
  //   _
  //   _
  //   |
  //   |
  //   |
  //   |
  //   |
  //   |
  //   |
  //   |
  //   |
  //   _
  //   _
  //   _
  //   _
  //   _
  //   Output Register:
  //   _
  //   _
  //   _
  //   _
  //   _
  //   Input/Output:
  //   _
  //   _
  //   _
  //   _
  //   _
  //   _
  //   _
  //   _
  //   _
  //   _
  //   _
  //   _
  //   _
  //   _
endmodule

module INPR (
  input  CLK,
  output [7:0] out_2
);

  Counter counter_1 (.load(1'b0), .count(1'b0), .Q(out_2), .clk(CLK), .clr(1'b0));  // open: D, carry

  // Other names for the same wires on the sheet: Out[7:0] = out_2

  // Notes on the sheet:
  //   _
  //   _
  //   _
  //   _
  //   _
  //   Output:
  //   Input Register:
  //   _
  //   _
  //   _
  //   _
  //   _
  //   _
  //   _
  //   _
endmodule

module SC (
  input  CLK,
  input  [3:0] In,
  input  T6,
  input  T5,
  input  T4,
  input  T2,
  input  D6,
  input  D5,
  input  D4,
  input  D3,
  input  D2,
  input  D1,
  input  D0,
  input  R,
  input  r_2,
  input  p,
  output [3:0] Out
);

  wire and_1_out, and_2_out, and_3_out, and_4_out, and_5_out, and_6_out, and_7_out, and_8_out, CLR, not_1_out;

  and and_1 (and_1_out, R, T2);
  and and_2 (and_2_out, D0, T5);
  and and_3 (and_3_out, D1, T5);
  and and_4 (and_4_out, D2, T5);
  and and_5 (and_5_out, D3, T4);
  and and_6 (and_6_out, D4, T4);
  and and_7 (and_7_out, D5, T5);
  and and_8 (and_8_out, D6, T6);
  or u_CLR (CLR, p, r_2, and_1_out, and_2_out, and_3_out, and_4_out, and_5_out, and_6_out, and_7_out, and_8_out);
  not not_1 (not_1_out, CLR);
  Counter #(.width(4), .max('hf)) counter_1 (
    .load(CLR), .D(In), .count(not_1_out), .Q(Out), .clk(CLK));  // open: carry, clr

  // Other names for the same wires on the sheet: r_t = r_2

  // Notes on the sheet:
  //   Control Gates:
  //   |
  //   |
  //   |
  //   |
  //   |
  //   |
  //   |
  //   |
  //   |
  //   |
  //   |
  //   |
  //   |
  //   |
  //   |
  //   |
  //   |
  //   |
  //   |
  //   _
  //   _
  //   _
  //   _
  //   _
  //   _
  //   Sequence Counter:
  //   _
  //   _
  //   _
  //   _
  //   Input/Output:
  //   _
  //   _
  //   _
  //   _
endmodule

module I (
  input  CLK,
  input  T2,
  input  R,
  input  IR_15,
  output out_5
);

  wire and_1_out, and_2_out, not_1_out, not_2_out, not_3_out, Reset, Set;

  not not_1 (not_1_out, R);
  and and_1 (and_1_out, not_1_out, T2);
  not not_2 (not_2_out, R);
  and and_2 (and_2_out, not_2_out, T2);
  not not_3 (not_3_out, IR_15);
  and u_Set (Set, and_1_out, IR_15);
  and u_Reset (Reset, and_2_out, not_3_out);
  J_K_Flip_Flop j_k_ff_1 (.J(Set), .clk(CLK), .K(Reset), .Q(out_5));  // open: Qn, preset, en, reset

  // Notes on the sheet:
  //   Control Gates:
  //   |
  //   |
  //   |
  //   |
  //   |
  //   |
  //   _
  //   |
  //   |
  //   |
  //   |
  //   |
  //   |
  //   |
  //   |
  //   _
  //   _
  //   _
  //   _
  //   _
  //   _
  //   Indirect flip-flop:
  //   _
  //   _
  //   _
  //   _
  //   _
  //   _
  //   _
  //   _
  //   _
  //   _
  //   _
  //   _
  //   _
  //   _
  //   _
  //   _
  //   _
  //   _
endmodule

module S (
  input  CLK,
  input  B0,
  input  r,
  output out_4
);

  wire Set;

  and u_Set (Set, r, B0);
  J_K_Flip_Flop j_k_ff_1 (.J(Set), .clk(CLK), .K(1'b0), .Q(out_4));  // open: Qn, preset, en, reset

  // Notes on the sheet:
  //   Control Gates:
  //   |
  //   |
  //   |
  //   |
  //   |
  //   |
  //   _
  //   _
  //   _
  //   _
  //   |
  //   |
  //   |
  //   |
  //   Start/Stop flip-flop:
  //   _
  //   _
  //   _
  //   _
  //   _
  //   _
  //   _
  //   _
  //   _
  //   _
  //   _
  //   _
endmodule

module E (
  input  CLK,
  input  E_Out,
  input  T5,
  input  D1,
  input  B10,
  input  B8,
  input  B7,
  input  B6,
  input  r,
  output out_10
);

  wire and_1_out, and_2_out, and_3_out, and_4_out, CLR, CME, EBit, ECarry, not_1_out, or_1_out, Reset, Set,
       UpdE;

  and and_1 (and_1_out, UpdE, E_Out);
  and u_CME (CME, r, B8);
  and and_2 (and_2_out, r, B7);
  and and_3 (and_3_out, r, B6);
  or u_Set (Set, CME, and_1_out);
  or u_EBit (EBit, and_2_out, and_3_out);
  and u_CLR (CLR, r, B10);
  and and_4 (and_4_out, UpdE, not_1_out);
  not not_1 (not_1_out, E_Out);
  or or_1 (or_1_out, CLR, and_4_out);
  and u_ECarry (ECarry, D1, T5);
  or u_Reset (Reset, CME, or_1_out);
  or u_UpdE (UpdE, ECarry, EBit);
  J_K_Flip_Flop j_k_ff_1 (.J(Set), .clk(CLK), .K(Reset), .Q(out_10));  // open: Qn, preset, en, reset

  // Other names for the same wires on the sheet: New_E = E_Out

  // Notes on the sheet:
  //   Control Gates:
  //   |
  //   |
  //   |
  //   |
  //   |
  //   |
  //   |
  //   |
  //   |
  //   |
  //   |
  //   |
  //   |
  //   |
  //   |
  //   |
  //   |
  //   |
  //   |
  //   _
  //   _
  //   _
  //   _
  //   _
  //   _
  //   _
  //   _
  //   _
  //   _
  //   Extended AC bit flip-flop:
  //   _
  //   _
  //   _
  //   _
  //   _
  //   _
  //   _
  //   _
  //   _
  //   _
  //   _
  //   _
  //   _
  //   _
  //   _
endmodule

module R (
  input  CLK,
  input  T0,
  input  T1,
  input  T2,
  input  R,
  input  IEN,
  input  FGI,
  input  FGO,
  output out_9
);

  wire not_1_out, not_2_out, not_3_out, or_1_out, Reset, Set;

  not not_1 (not_1_out, T0);
  not not_2 (not_2_out, T1);
  not not_3 (not_3_out, T2);
  or or_1 (or_1_out, FGI, FGO);
  and u_Reset (Reset, R, T2);
  and u_Set (Set, not_1_out, not_2_out, not_3_out, IEN, or_1_out);
  J_K_Flip_Flop j_k_ff_1 (.J(Set), .clk(CLK), .K(Reset), .Q(out_9));  // open: Qn, preset, en, reset

  // Notes on the sheet:
  //   Control Gates:
  //   |
  //   |
  //   |
  //   |
  //   |
  //   |
  //   _
  //   _
  //   _
  //   |
  //   |
  //   |
  //   |
  //   |
  //   |
  //   |
  //   |
  //   |
  //   |
  //   _
  //   _
  //   _
  //   _
  //   _
  //   Interrupt flip-flop:
  //   _
  //   _
  //   _
  //   _
  //   _
  //   _
  //   _
  //   _
  //   _
  //   _
  //   _
  //   _
  //   _
  //   _
  //   _
  //   _
  //   _
endmodule

module IEN (
  input  CLK,
  input  T2,
  input  B6,
  input  B7,
  input  p,
  input  R,
  output out_7
);

  wire and_1_out, and_2_out, Reset, Set;

  and and_1 (and_1_out, R, T2);
  and and_2 (and_2_out, p, B6);
  and u_SET (Set, p, B7);
  or CLR (Reset, and_1_out, and_2_out);
  J_K_Flip_Flop j_k_ff_1 (.J(Set), .clk(CLK), .K(Reset), .Q(out_7));  // open: Qn, preset, en, reset

  // Notes on the sheet:
  //   Control Gates:
  //   |
  //   |
  //   |
  //   |
  //   |
  //   |
  //   _
  //   _
  //   _
  //   _
  //   |
  //   |
  //   |
  //   |
  //   |
  //   |
  //   |
  //   |
  //   |
  //   |
  //   _
  //   _
  //   _
  //   _
  //   _
  //   Interrupt Flag flip-flop:
  //   _
  //   _
  //   _
  //   _
  //   _
  //   _
  //   _
  //   _
  //   _
  //   _
  //   _
  //   _
  //   _
  //   _
  //   _
  //   _
endmodule

module FGI (
  input  CLK,
  input  B11,
  input  p,
  output out_4
);

  wire Reset;

  and CLR (Reset, p, B11);
  J_K_Flip_Flop j_k_ff_1 (.J(1'b0), .clk(CLK), .K(Reset), .Q(out_4));  // open: Qn, preset, en, reset

  // Notes on the sheet:
  //   Control Gates:
  //   |
  //   |
  //   |
  //   |
  //   |
  //   |
  //   _
  //   |
  //   |
  //   |
  //   |
  //   |
  //   _
  //   _
  //   _
  //   _
  //   _
  //   Input Flag flip-flop:
  //   _
  //   _
  //   _
  //   _
  //   _
  //   _
  //   _
  //   _
  //   _
  //   _
  //   _
  //   _
  //   _
  //   _
  //   _
  //   _
  //   _
  //   _
  //   _
endmodule

module FGO (
  input  CLK,
  input  B10,
  input  p,
  output out_4
);

  wire Reset;

  and CLR (Reset, p, B10);
  J_K_Flip_Flop j_k_ff_1 (.J(1'b0), .clk(CLK), .K(Reset), .Q(out_4));  // open: Qn, preset, en, reset

  // Notes on the sheet:
  //   Control Gates:
  //   |
  //   |
  //   |
  //   |
  //   |
  //   |
  //   _
  //   |
  //   |
  //   |
  //   |
  //   |
  //   _
  //   _
  //   _
  //   _
  //   _
  //   Output Flag flip-flop:
  //   _
  //   _
  //   _
  //   _
  //   _
  //   _
  //   _
  //   _
  //   _
  //   _
  //   _
  //   _
  //   _
  //   _
  //   _
  //   _
  //   _
  //   _
  //   _
endmodule
